# Fritzing sketch sensor_package_pcb (saved by Fritzing 0.9.3b)
circuit board: 6.9215cm x 5.33756cm
breadboards: 1

parts:
  SIM800L = female pin header, 7 pins [form="♀ (female)"]
  S1 = Pushbutton [package="[THT]"]
  Button_Resistor = Resistor [tolerance=±5% resistance=2.2k package=THT]
  SIM800L_R1 = Resistor [tolerance=±5% resistance=150 package=THT]
  Blue_Resistor = Resistor [tolerance=±5% resistance=100 package=THT]
  SIM800L_R2 = Resistor [tolerance=±5% resistance=150 package=THT]
  Green_Resistor = Resistor [tolerance=±5% resistance=100 package=THT]
  Red_Resistor = Resistor [tolerance=±5% resistance=100 package=THT]
  DGS = female pin header, 8 pins [form="♀ (female)"]
  V2_1 = Arduino Uno (Rev3)
  LEDs = female pin header, 3 pins [form="♀ (female)"]
  Fan = female pin header, 2 pins [form="♀ (female)"]
  LED_GNDs = female pin header, 3 pins [form="♀ (female)"]
  C1 = Electrolytic Capacitor [capacitance=47µF voltage=50V package="200 mil [THT, electrolytic]"]

nets:
  N1: SIM800L.pin3, SIM800L_R2.Pin_0
  N2: SIM800L.pin4, SIM800L_R1.Pin_0
  N3: SIM800L.pin6, S1.Pin_1, S1.Pin_2, Button_Resistor.Pin_0, DGS.pin6, V2_1.GND, Fan.pin1, LED_GNDs.pin1, LED_GNDs.pin2, LED_GNDs.pin3, C1.-
  N4: SIM800L.pin7, V2_1.5V, Fan.pin2, C1.+
  N5: Button_Resistor.Pin_1, V2_1.D9_PWM
  N6: SIM800L_R1.Pin_1, V2_1.D11_PWM/MOSI
  N7: Blue_Resistor.Pin_0, LEDs.pin2
  N8: Blue_Resistor.Pin_1, V2_1.D6_PWM
  N9: SIM800L_R2.Pin_1, V2_1.D12/MISO
  N10: Green_Resistor.Pin_0, LEDs.pin3
  N11: Green_Resistor.Pin_1, V2_1.D7
  N12: Red_Resistor.Pin_0, LEDs.pin1
  N13: Red_Resistor.Pin_1, V2_1.D5_PWM
  N14: DGS.pin2, V2_1.D4
  N15: DGS.pin3, V2_1.D3_PWM
  N16: DGS.pin8, V2_1.3V3
