# Fritzing sketch sensor_shield (saved by Fritzing 0.9.3b)
circuit board: 6.9215cm x 5.33756cm
breadboards: 1

parts:
  DGS = female pin header, 8 pins [form="♀ (female)"]
  Fan = female pin header, 2 pins [form="♀ (female)"]
  1602A_(LCD) = female pin header, 16 pins [form="♀ (female)"]
  DS1307_(RTC) = female pin header, 5 pins [form="♀ (female)"]
  R1 = Trimmer Potentiometer [maximum_resistance=10kΩ package=THT]
  R2 = Resistor [tolerance=±5% resistance=1k package=THT]
  RFM95W_(Radio) = female pin header, 9 pins [form="♀ (female)"]
  RFM95W_(Radio)_-_BACK = female pin header, 5 pins [form="♀ (female)"]  # not connected
  V3_2 = Arduino Uno (Rev3)

nets:
  N1: DGS.pin2, V3_2.D8
  N2: DGS.pin3, V3_2.D7
  N3: DGS.pin6, Fan.pin1, 1602A_(LCD).pin1, 1602A_(LCD).pin5, 1602A_(LCD).pin16, DS1307_(RTC).pin1, R1.leg1, R1.leg2, RFM95W_(Radio).pin2, V3_2.GND
  N4: DGS.pin8, V3_2.3V3
  N5: Fan.pin2, 1602A_(LCD).pin2, DS1307_(RTC).pin2, RFM95W_(Radio).pin1, V3_2.5V
  N6: 1602A_(LCD).pin3, R1.wiper
  N7: 1602A_(LCD).pin4, V3_2.A0
  N8: 1602A_(LCD).pin6, V3_2.A1
  N9: 1602A_(LCD).pin11, V3_2.D9_PWM
  N10: 1602A_(LCD).pin12, V3_2.D10_PWM/SS
  N11: 1602A_(LCD).pin13, V3_2.D5_PWM
  N12: 1602A_(LCD).pin14, V3_2.A2
  N13: 1602A_(LCD).pin15, R2.Pin_1
  N14: DS1307_(RTC).pin3, V3_2.A4/SDA
  N15: DS1307_(RTC).pin4, V3_2.A5/SCL
  N16: R2.Pin_0, V3_2.A3
  N17: RFM95W_(Radio).pin4, V3_2.D3_PWM
  N18: RFM95W_(Radio).pin5, V3_2.D13/SCK
  N19: RFM95W_(Radio).pin6, V3_2.D12/MISO
  N20: RFM95W_(Radio).pin7, V3_2.D11_PWM/MOSI
  N21: RFM95W_(Radio).pin8, V3_2.D4
  N22: RFM95W_(Radio).pin9, V3_2.D2

notes:
  RX
  TX
  GND
  3.3v
  16
  V+
  1kΩ
  SDA
  SCL
  5V
  8
